# Fritzing sketch LINE_FOLLOWER1ST (saved by Fritzing 0.8.7b)

parts:
  S1 = H-Bridge with L298N
  Εξάρτημα1 = Arduino Uno (Rev3)
  M1 = DC Motor
  M2 = DC Motor
  VCC1 = Battery
  VCC2 = Battery
  Εξάρτημα2 = Max Power IR LED Kit
  Εξάρτημα3 = Max Power IR LED Kit
  Εξάρτημα4 = Max Power IR LED Kit
  S2 = Momentary Switch [package=tactile_switch_smd]

nets:
  12V: S1.12V, S1.GND, S2.1, S2.2
  N1: S1.ENA, Εξάρτημα1.D11_PWM/MOSI
  N2: S1.IN1, Εξάρτημα1.D2
  N3: S1.IN2, Εξάρτημα1.D3_PWM
  N4: S1.IN3, Εξάρτημα1.D4
  N5: S1.IN4, Εξάρτημα1.D5_PWM
  N6: S1.ENB, Εξάρτημα1.D10_PWM/SS
  N7: S1.M1-01, M1.pin_2
  N8: S1.M1-02, M1.pin_1
  N9: S1.M2-01, M2.pin_2
  N10: S1.M2-02, M2.pin_1
  VCC: Εξάρτημα1.5V, Εξάρτημα2.VCC, Εξάρτημα3.VCC, Εξάρτημα4.VCC
  GND: Εξάρτημα1.GND, Εξάρτημα2.GND, Εξάρτημα3.GND, Εξάρτημα4.GND
  N11: VCC1.-, VCC1.+, VCC2.-, VCC2.+, S2.3, S2.4

custom parts:
  H-Bridge with L298N: h-bridge
  Momentary Switch: Momentary Switch Button commonly used for reset or general input. Spark Fun Electronics SKU : COM-00097
